// Logisim project display1.circ as structural Verilog
module display (
  input  X,
  input  Y,
  input  W,
  input  Z,
  output G,
  output F,
  output E,
  output D,
  output C,
  output B,
  output A
);

  wire and_1_out, and_2_out, and_3_out, and_4_out, and_5_out, and_6_out, and_7_out, and_8_out, and_9_out,
       and_10_out, and_11_out, and_12_out, and_13_out, and_14_out, and_15_out, and_16_out, and_17_out,
       and_18_out, and_19_out, and_20_out, and_21_out, and_22_out, and_23_out, and_24_out, and_25_out,
       and_26_out, and_27_out, and_28_out, and_29_out, and_30_out, and_31_out, and_32_out, and_33_out,
       and_34_out, and_35_out, not_1_out, not_2_out, not_3_out, not_4_out, not_5_out, not_6_out, not_7_out,
       not_8_out, not_9_out, not_10_out, not_11_out, not_12_out, not_13_out, not_14_out, not_15_out,
       not_16_out, not_17_out, not_18_out, not_19_out, not_20_out, not_21_out, not_22_out, not_23_out,
       not_24_out, not_25_out, not_26_out, not_27_out, not_28_out, not_29_out, not_30_out, not_31_out,
       not_32_out, not_33_out, not_34_out, not_35_out, not_36_out, not_37_out, not_38_out, not_39_out,
       not_40_out, not_41_out, not_42_out, not_43_out, not_44_out;

  not not_1 (not_1_out, Y);
  and and_1 (and_1_out, not_1_out, W);
  and and_2 (and_2_out, W, not_2_out);
  not not_2 (not_2_out, Z);
  not not_3 (not_3_out, X);
  and and_3 (and_3_out, not_3_out, Y, not_4_out);
  not not_4 (not_4_out, W);
  and and_4 (and_4_out, X, not_5_out);
  not not_5 (not_5_out, Y);
  and and_5 (and_5_out, X, Z);
  not not_6 (not_6_out, W);
  and and_6 (and_6_out, not_6_out, not_7_out);
  not not_7 (not_7_out, Z);
  not not_8 (not_8_out, X);
  and and_7 (and_7_out, not_8_out, Y, not_9_out);
  not not_9 (not_9_out, W);
  and and_8 (and_8_out, Y, not_10_out);
  not not_10 (not_10_out, Z);
  and and_9 (and_9_out, X, not_11_out);
  not not_11 (not_11_out, Y);
  and and_10 (and_10_out, X, W);
  not not_12 (not_12_out, Y);
  and and_11 (and_11_out, not_12_out, not_13_out);
  not not_13 (not_13_out, Z);
  and and_12 (and_12_out, W, not_14_out);
  not not_14 (not_14_out, Z);
  and and_13 (and_13_out, X, W);
  and and_14 (and_14_out, X, Y);
  not not_15 (not_15_out, X);
  not not_16 (not_16_out, Y);
  and and_15 (and_15_out, not_15_out, not_16_out, not_17_out);
  not not_17 (not_17_out, Z);
  not not_18 (not_18_out, Y);
  and and_16 (and_16_out, not_18_out, W, Z);
  not not_19 (not_19_out, W);
  and and_17 (and_17_out, Y, not_19_out, Z);
  and and_18 (and_18_out, Y, W, not_20_out);
  not not_20 (not_20_out, Z);
  not not_21 (not_21_out, W);
  and and_19 (and_19_out, X, not_21_out, not_22_out);
  not not_22 (not_22_out, Z);
  not not_23 (not_23_out, X);
  and and_20 (and_20_out, not_23_out, not_24_out);
  not not_24 (not_24_out, W);
  not not_25 (not_25_out, X);
  and and_21 (and_21_out, not_25_out, Z);
  not not_26 (not_26_out, W);
  and and_22 (and_22_out, not_26_out, Z);
  not not_27 (not_27_out, X);
  and and_23 (and_23_out, not_27_out, Y);
  and and_24 (and_24_out, X, not_28_out);
  not not_28 (not_28_out, Y);
  not not_29 (not_29_out, X);
  and and_25 (and_25_out, not_29_out, not_30_out);
  not not_30 (not_30_out, Y);
  not not_31 (not_31_out, X);
  not not_32 (not_32_out, W);
  and and_26 (and_26_out, not_31_out, not_32_out, not_33_out);
  not not_33 (not_33_out, Z);
  not not_34 (not_34_out, Y);
  and and_27 (and_27_out, not_34_out, not_35_out);
  not not_35 (not_35_out, Z);
  not not_36 (not_36_out, X);
  and and_28 (and_28_out, not_36_out, W, Z);
  not not_37 (not_37_out, W);
  and and_29 (and_29_out, X, not_37_out, Z);
  not not_38 (not_38_out, Y);
  and and_30 (and_30_out, not_38_out, not_39_out);
  not not_39 (not_39_out, Z);
  not not_40 (not_40_out, X);
  and and_31 (and_31_out, not_40_out, W);
  not not_41 (not_41_out, X);
  and and_32 (and_32_out, not_41_out, Y, Z);
  and and_33 (and_33_out, Y, W);
  not not_42 (not_42_out, Y);
  and and_34 (and_34_out, X, not_42_out, not_43_out);
  not not_43 (not_43_out, W);
  and and_35 (and_35_out, X, not_44_out);
  not not_44 (not_44_out, Z);
  or or_1 (G, and_1_out, and_2_out, and_3_out, and_4_out, and_5_out);
  or or_2 (F, and_6_out, and_7_out, and_8_out, and_9_out, and_10_out);
  or or_3 (E, and_11_out, and_12_out, and_13_out, and_14_out);
  or or_4 (D, and_15_out, and_16_out, and_17_out, and_18_out, and_19_out);
  or or_5 (C, and_20_out, and_21_out, and_22_out, and_23_out, and_24_out);
  or or_6 (B, and_25_out, and_26_out, and_27_out, and_28_out, and_29_out);
  or or_7 (A, and_30_out, and_31_out, and_32_out, and_33_out, and_34_out, and_35_out);
  _7_Segment_Display u_7_segment_display_1 (.g(G), .f(F), .a(A), .b(B), .e(E), .d(D), .c(C));  // open: dp
endmodule
