// Logisim project x,y, y elevador.circ as structural Verilog: 3 circuits, main circuit X < Y
module X___Y (
  input  \X¹ ,
  input  \X⁰ ,
  input  \Y¹ ,
  input  \Y⁰ ,
  output \f_x¹_x⁰_y¹_y⁰ 
);

  wire not_1_out, not_2_out, not_3_out, not_4_out, \nX¹_nX⁰Y⁰_out , \nX¹Y¹_out , \nX⁰Y¹Y⁰_out ;

  not not_1 (not_1_out, \X¹ );
  not not_2 (not_2_out, \X⁰ );
  not not_3 (not_3_out, \Y⁰ );
  not not_4 (not_4_out, \Y¹ );
  and \nX¹_nX⁰Y⁰  (\nX¹_nX⁰Y⁰_out , not_1_out, not_2_out, \Y⁰ );
  and \nX⁰Y¹Y⁰  (\nX⁰Y¹Y⁰_out , not_2_out, \Y¹ , \Y⁰ );
  and \nX¹Y¹  (\nX¹Y¹_out , not_1_out, \Y¹ );
  or or_1 (\f_x¹_x⁰_y¹_y⁰ , \nX¹_nX⁰Y⁰_out , \nX⁰Y¹Y⁰_out , \nX¹Y¹_out );

  // Notes on the sheet:
  //   ¬X¹¬X⁰Y⁰ + ¬X⁰Y¹Y⁰ + ¬X¹Y¹
endmodule

module X____Y (
  input  \X¹ ,
  input  \X⁰ ,
  input  \Y¹ ,
  input  \Y⁰ ,
  output \f_x¹_x⁰_y¹_y⁰ 
);

  wire and_1_out, and_2_out, and_3_out, and_4_out, not_1_out, not_2_out, not_3_out, not_4_out;

  not not_1 (not_1_out, \X¹ );
  not not_2 (not_2_out, \X⁰ );
  not not_3 (not_3_out, \Y⁰ );
  not not_4 (not_4_out, \Y¹ );
  and and_1 (and_1_out, not_1_out, not_2_out, not_4_out, not_3_out);
  and and_2 (and_2_out, not_1_out, \X⁰ , not_4_out, \Y⁰ );
  and and_3 (and_3_out, \X¹ , not_2_out, \Y¹ , not_3_out);
  and and_4 (and_4_out, \X¹ , \X⁰ , \Y¹ , \Y⁰ );
  or or_1 (\f_x¹_x⁰_y¹_y⁰ , and_1_out, and_2_out, and_3_out, and_4_out);

  // Notes on the sheet:
  //   ¬X¹¬X⁰¬Y¹¬Y⁰ 
  //    ¬X¹X⁰¬Y¹Y⁰ 
  //    X¹¬X⁰Y¹¬Y⁰ 
  //   X¹X⁰Y¹Y⁰
  //   ¬X¹¬X⁰¬Y¹¬Y⁰ + ¬X¹X⁰¬Y¹Y⁰ + X¹¬X⁰Y¹¬Y⁰ + X¹X⁰Y¹Y⁰
endmodule

module Elevador (
  input  \P¹ ,
  input  \P⁰ ,
  input  \B¹ ,
  input  \B⁰ ,
  output \Fd¹_p¹_p⁰_b¹_b⁰ ,
  output \Fd⁰_p¹_p⁰_b¹_b⁰ ,
  output \Fn¹_p¹_p⁰_b¹_b⁰ ,
  output \Fn⁰_p¹_p⁰_b¹_b⁰ 
);

  wire and_1_out, and_2_out, and_3_out, and_4_out, and_5_out, and_6_out, and_7_out, and_8_out, and_9_out,
       and_10_out, and_11_out, and_12_out, not_1_out, not_2_out, not_3_out, not_4_out;

  not not_1 (not_1_out, \P¹ );
  not not_2 (not_2_out, \B¹ );
  not not_3 (not_3_out, \P⁰ );
  not not_4 (not_4_out, \B⁰ );
  or or_1 (\Fd¹_p¹_p⁰_b¹_b⁰ , and_1_out, and_2_out, and_3_out);
  and and_1 (and_1_out, not_1_out, \B¹ );
  and and_2 (and_2_out, not_1_out, not_3_out, \B⁰ );
  and and_3 (and_3_out, not_3_out, \B¹ , \B⁰ );
  and and_4 (and_4_out, \P¹ , not_2_out);
  and and_5 (and_5_out, \P⁰ , not_2_out, not_4_out);
  and and_6 (and_6_out, \P¹ , \P⁰ , not_4_out);
  and and_7 (and_7_out, \P¹ , not_2_out, not_4_out);
  and and_8 (and_8_out, \P¹ , \P⁰ , not_2_out);
  and and_9 (and_9_out, not_1_out, \B¹ , \B⁰ );
  and and_10 (and_10_out, not_1_out, not_3_out, \B¹ );
  and and_11 (and_11_out, \P⁰ , not_4_out);
  and and_12 (and_12_out, not_3_out, \B⁰ );
  or or_2 (\Fd⁰_p¹_p⁰_b¹_b⁰ , and_4_out, and_5_out, and_6_out);
  or or_3 (\Fn¹_p¹_p⁰_b¹_b⁰ , and_7_out, and_8_out, and_9_out, and_10_out);
  X___Y x_y_1 (.\X¹ (and_9_out), .\X⁰ (and_10_out));  // open: Y¹, Y⁰, f_x¹_x⁰_y¹_y⁰
  or or_4 (\Fn⁰_p¹_p⁰_b¹_b⁰ , and_11_out, and_12_out);

  // Notes on the sheet:
  //   0  1 --- 1 piso
  //   1  0 --- 2 pisos
  //   1  1 --- 3 pisos
  //   Pines de entrada
  //   0  1 --- piso 1
  //   1  0 --- piso 2
  //   1  1 --- piso 3
  //   Boton del piso seleccionado
  //   B¹   B⁰  --- que representa
  //   0   0 --- piso 1
  //   0  1 --- piso 0 o planta baja
  //   1  0 --- piso 2
  //   1   1 --- piso 3
  //   Pines de salida
  //   Direccion
  //   Fd¹(p¹,p⁰,b¹,b⁰)    Fd⁰(p¹,p⁰,b¹,b⁰)  --- que representa
  //   0  0 --- no se mueve
  //   1  0 --- sube
  //   0  1 --- baja
  //   Pisos que se dezplaza
  //   Fn¹(p¹,p⁰,b¹,b⁰)    Fn⁰(p¹,p⁰,b¹,b⁰)  --- que representa
  //   0  0 --- 0 pisos o no se mueve
  //   Piso en el que se encuentra el elevador
  //   P¹    P⁰  --- que representa
  //   0   0  --- piso 0 o planta baja
endmodule
