// Logisim project practica03.circ as structural Verilog: 12 circuits, main circuit AND Y OR
module AND_Y_OR (
  input  in_1,
  input  in_2,
  input  in_3,
  output out_4
);

  wire and_1_out, or_1_out;

  or or_1 (or_1_out, in_1, in_2);
  and and_1 (and_1_out, in_1, in_2);
  Multiplexer #(.enable("false")) multiplexer_1 (.in0(and_1_out), .in1(or_1_out), .out(out_4), .sel(in_3));
endmodule

module Sumador (
  input  C_in,
  input  A,
  input  B,
  output salida,
  output C_out
);

  wire and_1_out, and_2_out, and_3_out, and_4_out, and_5_out, and_6_out, and_7_out, not_1_out, not_2_out,
       not_3_out;

  not not_1 (not_1_out, C_in);
  not not_2 (not_2_out, A);
  not not_3 (not_3_out, B);
  and and_1 (and_1_out, C_in, B);
  and and_2 (and_2_out, A, B);
  and and_3 (and_3_out, C_in, A);
  and and_4 (and_4_out, C_in, not_2_out, not_3_out);
  and and_5 (and_5_out, not_1_out, not_2_out, B);
  and and_6 (and_6_out, C_in, A, B);
  and and_7 (and_7_out, not_1_out, A, not_3_out);
  or or_1 (C_out, and_1_out, and_2_out, and_3_out);
  or or_2 (salida, and_4_out, and_5_out, and_6_out, and_7_out);
endmodule

module ALU_1_bit_sumador (
  input  a,
  input  b,
  input  [1:0] Op,
  input  c_in,
  output salida,
  output c_out
);

  wire and_1_out, or_1_out, sumador_1_c_out, sumador_1_salida;

  Sumador sumador_1 (.C_in(c_in), .A(a), .B(b), .C_out(sumador_1_c_out), .salida(sumador_1_salida));
  or or_1 (or_1_out, a, b);
  and and_1 (and_1_out, a, b);
  Multiplexer #(.select(2), .disabled(0), .enable("false")) multiplexer_1 (
    .in0(and_1_out), .in1(or_1_out), .in2(sumador_1_salida), .out(salida), .sel(Op));  // open: in3
  and and_2 (c_out, ~Op[0], Op[1], sumador_1_c_out);  // AND_Gate
endmodule

module ALU_8_bits_sumador (
  input  C_in,
  input  [1:0] Op,
  input  [7:0] A,
  input  [7:0] B,
  output [7:0] Salida,
  output C_out
);

  wire alu_1_bit_sumador_1_c_out, alu_1_bit_sumador_2_c_out, alu_1_bit_sumador_3_c_out,
       alu_1_bit_sumador_4_c_out, alu_1_bit_sumador_5_c_out, alu_1_bit_sumador_6_c_out,
       alu_1_bit_sumador_7_c_out;

  ALU_1_bit_sumador alu_1_bit_sumador_1 (
    .a(A[0]), .b(B[0]), .Op(Op), .c_in(C_in), .salida(Salida[0]), .c_out(alu_1_bit_sumador_1_c_out));
  ALU_1_bit_sumador alu_1_bit_sumador_2 (
    .a(A[1]), .b(B[1]), .Op(Op), .c_in(alu_1_bit_sumador_1_c_out), .salida(Salida[1]),
    .c_out(alu_1_bit_sumador_2_c_out));
  ALU_1_bit_sumador alu_1_bit_sumador_3 (
    .a(A[2]), .b(B[2]), .Op(Op), .c_in(alu_1_bit_sumador_2_c_out), .salida(Salida[2]),
    .c_out(alu_1_bit_sumador_3_c_out));
  ALU_1_bit_sumador alu_1_bit_sumador_4 (
    .a(A[3]), .b(B[3]), .Op(Op), .c_in(alu_1_bit_sumador_3_c_out), .salida(Salida[3]),
    .c_out(alu_1_bit_sumador_4_c_out));
  ALU_1_bit_sumador alu_1_bit_sumador_5 (
    .a(A[4]), .b(B[4]), .Op(Op), .c_in(alu_1_bit_sumador_4_c_out), .salida(Salida[4]),
    .c_out(alu_1_bit_sumador_5_c_out));
  ALU_1_bit_sumador alu_1_bit_sumador_6 (
    .a(A[5]), .b(B[5]), .Op(Op), .c_in(alu_1_bit_sumador_5_c_out), .salida(Salida[5]),
    .c_out(alu_1_bit_sumador_6_c_out));
  ALU_1_bit_sumador alu_1_bit_sumador_7 (
    .a(A[6]), .b(B[6]), .Op(Op), .c_in(alu_1_bit_sumador_6_c_out), .salida(Salida[6]),
    .c_out(alu_1_bit_sumador_7_c_out));
  ALU_1_bit_sumador alu_1_bit_sumador_8 (
    .a(A[7]), .b(B[7]), .Op(Op), .c_in(alu_1_bit_sumador_7_c_out), .salida(Salida[7]), .c_out(C_out));
endmodule

module ALU_1_bit_Resta (
  input  a,
  input  b,
  input  comp1,
  input  [1:0] Op,
  input  c_in,
  output salida,
  output c_out
);

  wire and_1_out, multiplexer_1_out, not_1_out, or_1_out, sumador_1_c_out, sumador_1_salida;

  not not_1 (not_1_out, b);
  Multiplexer #(.enable("false")) multiplexer_1 (.in0(b), .in1(not_1_out), .out(multiplexer_1_out), .sel(comp1));
  Sumador sumador_1 (.C_in(c_in), .A(a), .B(multiplexer_1_out), .C_out(sumador_1_c_out), .salida(sumador_1_salida));
  or or_1 (or_1_out, a, multiplexer_1_out);
  and and_1 (and_1_out, a, multiplexer_1_out);
  Multiplexer #(.select(2), .disabled(0), .enable("false")) multiplexer_2 (
    .in0(and_1_out), .in1(or_1_out), .in2(sumador_1_salida), .out(salida), .sel(Op));  // open: in3
  and and_2 (c_out, ~Op[0], Op[1], sumador_1_c_out);  // AND_Gate
endmodule

module ALU_8_bits_resta (
  input  [1:0] Op,
  input  [7:0] A,
  input  [7:0] B,
  output [7:0] Salida,
  output C_out
);

  wire alu_1_bit_resta_1_c_out, alu_1_bit_resta_2_c_out, alu_1_bit_resta_3_c_out, alu_1_bit_resta_4_c_out,
       alu_1_bit_resta_5_c_out, alu_1_bit_resta_6_c_out, alu_1_bit_resta_7_c_out, alu_1_bit_resta_8_c_out,
       and_1_out, controlador_resta_1_comp, controlador_resta_1_in, not_1_out;
  wire [1:0] controlador_resta_1_b;

  Controlador_resta controlador_resta_1 (
    .X(Op[1]), .Y(Op[0]), .in(controlador_resta_1_in), .Comp(controlador_resta_1_comp),
    .A(controlador_resta_1_b[1]), .B(controlador_resta_1_b[0]));
  and and_1 (and_1_out, Op[0], Op[1]);
  ALU_1_bit_Resta alu_1_bit_resta_1 (
    .a(A[0]), .b(B[0]), .Op(controlador_resta_1_b), .c_in(controlador_resta_1_in), .salida(Salida[0]),
    .comp1(controlador_resta_1_comp), .c_out(alu_1_bit_resta_1_c_out));
  ALU_1_bit_Resta alu_1_bit_resta_2 (
    .a(A[1]), .b(B[1]), .Op(controlador_resta_1_b), .c_in(alu_1_bit_resta_1_c_out), .salida(Salida[1]),
    .comp1(controlador_resta_1_comp), .c_out(alu_1_bit_resta_2_c_out));
  ALU_1_bit_Resta alu_1_bit_resta_3 (
    .a(A[2]), .b(B[2]), .Op(controlador_resta_1_b), .c_in(alu_1_bit_resta_2_c_out), .salida(Salida[2]),
    .comp1(controlador_resta_1_comp), .c_out(alu_1_bit_resta_3_c_out));
  ALU_1_bit_Resta alu_1_bit_resta_4 (
    .a(A[3]), .b(B[3]), .Op(controlador_resta_1_b), .c_in(alu_1_bit_resta_3_c_out), .salida(Salida[3]),
    .comp1(controlador_resta_1_comp), .c_out(alu_1_bit_resta_4_c_out));
  ALU_1_bit_Resta alu_1_bit_resta_5 (
    .a(A[4]), .b(B[4]), .Op(controlador_resta_1_b), .c_in(alu_1_bit_resta_4_c_out), .salida(Salida[4]),
    .comp1(controlador_resta_1_comp), .c_out(alu_1_bit_resta_5_c_out));
  ALU_1_bit_Resta alu_1_bit_resta_6 (
    .a(A[5]), .b(B[5]), .Op(controlador_resta_1_b), .c_in(alu_1_bit_resta_5_c_out), .salida(Salida[5]),
    .comp1(controlador_resta_1_comp), .c_out(alu_1_bit_resta_6_c_out));
  ALU_1_bit_Resta alu_1_bit_resta_7 (
    .a(A[6]), .b(B[6]), .Op(controlador_resta_1_b), .c_in(alu_1_bit_resta_6_c_out), .salida(Salida[6]),
    .comp1(controlador_resta_1_comp), .c_out(alu_1_bit_resta_7_c_out));
  ALU_1_bit_Resta alu_1_bit_resta_8 (
    .a(A[7]), .b(B[7]), .Op(controlador_resta_1_b), .c_in(alu_1_bit_resta_7_c_out), .salida(Salida[7]),
    .comp1(controlador_resta_1_comp), .c_out(alu_1_bit_resta_8_c_out));
  Multiplexer #(.enable("false")) multiplexer_1 (
    .in0(alu_1_bit_resta_8_c_out), .in1(not_1_out), .out(C_out), .sel(and_1_out));
  not not_1 (not_1_out, alu_1_bit_resta_8_c_out);
endmodule

module Controlador_resta (
  input  X,
  input  Y,
  output in,
  output Comp,
  output A,
  output B
);

  wire not_1_out;

  and and_1 (in, X, Y);
  and and_2 (Comp, X, Y);
  not not_1 (not_1_out, X);
  and and_3 (B, not_1_out, Y);

  assign A = X;
endmodule

module ALU_8_bits_igualdad (
  input  [2:0] Op,
  input  [7:0] A,
  input  [7:0] B,
  output [7:0] Salida,
  output C_out
);

  wire alu_1_bit_resta_1_c_out, alu_1_bit_resta_2_c_out, alu_1_bit_resta_3_c_out, alu_1_bit_resta_4_c_out,
       alu_1_bit_resta_5_c_out, alu_1_bit_resta_6_c_out, alu_1_bit_resta_7_c_out, alu_1_bit_resta_8_c_out,
       and_1_out, and_3_out, controlador_igualdad_1_cin, controlador_igualdad_1_comp, multiplexer_1_out,
       not_1_out, not_2_out;
  wire [1:0] controlador_igualdad_1_op0;
  wire [7:0] alu_1_bit_resta_1_salida;
  wire [7:7] and_2_out;

  Controlador_igualdad controlador_igualdad_1 (
    .X(Op[2]), .Y(Op[1]), .Z(Op[0]), .Cin(controlador_igualdad_1_cin), .OP1(controlador_igualdad_1_op0[1]),
    .OP0(controlador_igualdad_1_op0[0]), .Comp(controlador_igualdad_1_comp));
  and and_1 (and_1_out, ~Op[2], Op[1], Op[0]);  // AND_Gate
  ALU_1_bit_Resta alu_1_bit_resta_1 (
    .a(A[0]), .b(B[0]), .Op(controlador_igualdad_1_op0), .c_in(controlador_igualdad_1_cin),
    .salida(alu_1_bit_resta_1_salida[0]), .comp1(controlador_igualdad_1_comp), .c_out(alu_1_bit_resta_1_c_out));
  ALU_1_bit_Resta alu_1_bit_resta_2 (
    .a(A[1]), .b(B[1]), .Op(controlador_igualdad_1_op0), .c_in(alu_1_bit_resta_1_c_out),
    .salida(alu_1_bit_resta_1_salida[1]), .comp1(controlador_igualdad_1_comp), .c_out(alu_1_bit_resta_2_c_out));
  ALU_1_bit_Resta alu_1_bit_resta_3 (
    .a(A[2]), .b(B[2]), .Op(controlador_igualdad_1_op0), .c_in(alu_1_bit_resta_2_c_out),
    .salida(alu_1_bit_resta_1_salida[2]), .comp1(controlador_igualdad_1_comp), .c_out(alu_1_bit_resta_3_c_out));
  ALU_1_bit_Resta alu_1_bit_resta_4 (
    .a(A[3]), .b(B[3]), .Op(controlador_igualdad_1_op0), .c_in(alu_1_bit_resta_3_c_out),
    .salida(alu_1_bit_resta_1_salida[3]), .comp1(controlador_igualdad_1_comp), .c_out(alu_1_bit_resta_4_c_out));
  ALU_1_bit_Resta alu_1_bit_resta_5 (
    .a(A[4]), .b(B[4]), .Op(controlador_igualdad_1_op0), .c_in(alu_1_bit_resta_4_c_out),
    .salida(alu_1_bit_resta_1_salida[4]), .comp1(controlador_igualdad_1_comp), .c_out(alu_1_bit_resta_5_c_out));
  ALU_1_bit_Resta alu_1_bit_resta_6 (
    .a(A[5]), .b(B[5]), .Op(controlador_igualdad_1_op0), .c_in(alu_1_bit_resta_5_c_out),
    .salida(alu_1_bit_resta_1_salida[5]), .comp1(controlador_igualdad_1_comp), .c_out(alu_1_bit_resta_6_c_out));
  ALU_1_bit_Resta alu_1_bit_resta_7 (
    .a(A[6]), .b(B[6]), .Op(controlador_igualdad_1_op0), .c_in(alu_1_bit_resta_6_c_out),
    .salida(alu_1_bit_resta_1_salida[6]), .comp1(controlador_igualdad_1_comp), .c_out(alu_1_bit_resta_7_c_out));
  ALU_1_bit_Resta alu_1_bit_resta_8 (
    .a(A[7]), .b(B[7]), .Op(controlador_igualdad_1_op0), .c_in(alu_1_bit_resta_7_c_out),
    .salida(alu_1_bit_resta_1_salida[7]), .comp1(controlador_igualdad_1_comp), .c_out(alu_1_bit_resta_8_c_out));
  and and_2 (and_2_out[7], ~alu_1_bit_resta_1_salida[0], ~alu_1_bit_resta_1_salida[1], ~alu_1_bit_resta_1_salida[2], ~alu_1_bit_resta_1_salida[3], ~alu_1_bit_resta_1_salida[4], ~alu_1_bit_resta_1_salida[5], ~alu_1_bit_resta_1_salida[6], ~alu_1_bit_resta_1_salida[7]);  // AND_Gate
  not not_1 (not_1_out, alu_1_bit_resta_8_c_out);
  and and_3 (and_3_out, Op[2], ~Op[1], Op[0]);  // AND_Gate
  Multiplexer multiplexer_1 (
    .in0(alu_1_bit_resta_8_c_out), .in1(not_1_out), .out(multiplexer_1_out), .sel(and_3_out));  // open: en
  not not_2 (not_2_out, and_1_out);
  Multiplexer multiplexer_2 (.in0(multiplexer_1_out), .in1(not_2_out), .out(C_out), .sel(and_1_out));  // open: en
  Multiplexer #(.width(8)) multiplexer_3 (
    .in0(alu_1_bit_resta_1_salida), .in1({8{and_2_out[7]}}), .out(Salida), .sel(and_1_out));  // open: en
endmodule

module Controlador_igualdad (
  input  X,
  input  Y,
  input  Z,
  output Cin,
  output OP1,
  output OP0,
  output Comp
);

  wire and_1_out, and_2_out, and_3_out, and_4_out, and_6_out, and_7_out, not_1_out, not_2_out, not_3_out,
       not_4_out, not_5_out, not_6_out, not_7_out, not_8_out;

  not not_1 (not_1_out, X);
  not not_2 (not_2_out, Y);
  not not_3 (not_3_out, X);
  not not_4 (not_4_out, Y);
  not not_5 (not_5_out, X);
  not not_6 (not_6_out, Y);
  not not_7 (not_7_out, X);
  not not_8 (not_8_out, Y);
  and and_1 (and_1_out, not_1_out, Y, Z);
  and and_2 (and_2_out, X, not_2_out, Z);
  and and_3 (and_3_out, not_3_out, Y, Z);
  and and_4 (and_4_out, X, not_4_out);
  and and_5 (OP0, not_5_out, not_6_out, Z);
  and and_6 (and_6_out, not_7_out, Y, Z);
  and and_7 (and_7_out, X, not_8_out, Z);
  or or_1 (Cin, and_1_out, and_2_out);
  or or_2 (OP1, and_3_out, and_4_out);
  or or_3 (Comp, and_6_out, and_7_out);
endmodule

module ALU_8_bits_completa (
  input  [2:0] Op,
  input  [7:0] A,
  input  [7:0] B,
  output [7:0] Salida,
  output C_out
);

  wire alu_1_bit_resta_1_c_out, alu_1_bit_resta_2_c_out, alu_1_bit_resta_3_c_out, alu_1_bit_resta_4_c_out,
       alu_1_bit_resta_5_c_out, alu_1_bit_resta_6_c_out, alu_1_bit_resta_7_c_out, alu_1_bit_resta_8_c_out,
       and_1_out, and_2_out, and_4_out, controlador_op_1_cin, controlador_op_1_comp, multiplexer_1_out,
       not_1_out, not_10_out;
  wire [1:0] controlador_op_1_op0;
  wire [7:0] alu_1_bit_resta_1_salida, multiplexer_3_out, not_2_out;
  wire [7:7] and_3_out;

  Controlador_OP controlador_op_1 (
    .X(Op[2]), .Y(Op[1]), .Z(Op[0]), .Cin(controlador_op_1_cin), .OP1(controlador_op_1_op0[1]),
    .OP0(controlador_op_1_op0[0]), .Comp(controlador_op_1_comp));
  and and_1 (and_1_out, ~Op[2], Op[1], Op[0]);  // AND_Gate
  and and_2 (and_2_out, ~Op[2], Op[1], ~Op[0]);  // AND_Gate
  ALU_1_bit_Resta alu_1_bit_resta_1 (
    .a(A[0]), .b(B[0]), .Op(controlador_op_1_op0), .c_in(controlador_op_1_cin),
    .salida(alu_1_bit_resta_1_salida[0]), .comp1(controlador_op_1_comp), .c_out(alu_1_bit_resta_1_c_out));
  ALU_1_bit_Resta alu_1_bit_resta_2 (
    .a(A[1]), .b(B[1]), .Op(controlador_op_1_op0), .c_in(alu_1_bit_resta_1_c_out),
    .salida(alu_1_bit_resta_1_salida[1]), .comp1(controlador_op_1_comp), .c_out(alu_1_bit_resta_2_c_out));
  ALU_1_bit_Resta alu_1_bit_resta_3 (
    .a(A[2]), .b(B[2]), .Op(controlador_op_1_op0), .c_in(alu_1_bit_resta_2_c_out),
    .salida(alu_1_bit_resta_1_salida[2]), .comp1(controlador_op_1_comp), .c_out(alu_1_bit_resta_3_c_out));
  ALU_1_bit_Resta alu_1_bit_resta_4 (
    .a(A[3]), .b(B[3]), .Op(controlador_op_1_op0), .c_in(alu_1_bit_resta_3_c_out),
    .salida(alu_1_bit_resta_1_salida[3]), .comp1(controlador_op_1_comp), .c_out(alu_1_bit_resta_4_c_out));
  ALU_1_bit_Resta alu_1_bit_resta_5 (
    .a(A[4]), .b(B[4]), .Op(controlador_op_1_op0), .c_in(alu_1_bit_resta_4_c_out),
    .salida(alu_1_bit_resta_1_salida[4]), .comp1(controlador_op_1_comp), .c_out(alu_1_bit_resta_5_c_out));
  ALU_1_bit_Resta alu_1_bit_resta_6 (
    .a(A[5]), .b(B[5]), .Op(controlador_op_1_op0), .c_in(alu_1_bit_resta_5_c_out),
    .salida(alu_1_bit_resta_1_salida[5]), .comp1(controlador_op_1_comp), .c_out(alu_1_bit_resta_6_c_out));
  ALU_1_bit_Resta alu_1_bit_resta_7 (
    .a(A[6]), .b(B[6]), .Op(controlador_op_1_op0), .c_in(alu_1_bit_resta_6_c_out),
    .salida(alu_1_bit_resta_1_salida[6]), .comp1(controlador_op_1_comp), .c_out(alu_1_bit_resta_7_c_out));
  ALU_1_bit_Resta alu_1_bit_resta_8 (
    .a(A[7]), .b(B[7]), .Op(controlador_op_1_op0), .c_in(alu_1_bit_resta_7_c_out),
    .salida(alu_1_bit_resta_1_salida[7]), .comp1(controlador_op_1_comp), .c_out(alu_1_bit_resta_8_c_out));
  and and_3 (and_3_out[7], ~alu_1_bit_resta_1_salida[0], ~alu_1_bit_resta_1_salida[1], ~alu_1_bit_resta_1_salida[2], ~alu_1_bit_resta_1_salida[3], ~alu_1_bit_resta_1_salida[4], ~alu_1_bit_resta_1_salida[5], ~alu_1_bit_resta_1_salida[6], ~alu_1_bit_resta_1_salida[7]);  // AND_Gate
  not not_1 (not_1_out, alu_1_bit_resta_8_c_out);
  Multiplexer multiplexer_1 (
    .in0(alu_1_bit_resta_8_c_out), .in1(not_1_out), .out(multiplexer_1_out), .sel(and_4_out));  // open: en
  and and_4 (and_4_out, Op[2], ~Op[1], Op[0]);  // AND_Gate
  not not_2 (not_2_out[0], alu_1_bit_resta_1_salida[0]);
  not not_3 (not_2_out[1], alu_1_bit_resta_1_salida[1]);
  not not_4 (not_2_out[2], alu_1_bit_resta_1_salida[2]);
  not not_5 (not_2_out[3], alu_1_bit_resta_1_salida[3]);
  not not_6 (not_2_out[4], alu_1_bit_resta_1_salida[4]);
  not not_7 (not_2_out[5], alu_1_bit_resta_1_salida[5]);
  not not_8 (not_2_out[6], alu_1_bit_resta_1_salida[6]);
  not not_9 (not_2_out[7], alu_1_bit_resta_1_salida[7]);
  Multiplexer multiplexer_2 (.in0(multiplexer_1_out), .in1(not_10_out), .out(C_out), .sel(and_1_out));  // open: en
  not not_10 (not_10_out, and_1_out);
  Multiplexer #(.width(8)) multiplexer_3 (
    .in0(alu_1_bit_resta_1_salida), .in1({8{and_3_out[7]}}), .out(multiplexer_3_out), .sel(and_1_out));  // open: en
  Multiplexer #(.width(8)) multiplexer_4 (
    .in0(multiplexer_3_out), .in1(not_2_out), .out(Salida), .sel(and_2_out));  // open: en
endmodule

module Controlador_OP (
  input  X,
  input  Y,
  input  Z,
  output Cin,
  output OP1,
  output OP0,
  output Comp
);

  wire and_1_out, and_2_out, and_3_out, and_4_out, and_5_out, and_6_out, and_7_out, and_8_out, not_1_out,
       not_2_out, not_3_out, not_4_out, not_5_out, not_6_out, not_7_out, not_8_out, not_9_out, not_10_out;

  not not_1 (not_1_out, X);
  not not_2 (not_2_out, Y);
  not not_3 (not_3_out, X);
  not not_4 (not_4_out, Y);
  not not_5 (not_5_out, X);
  not not_6 (not_6_out, Y);
  not not_7 (not_7_out, X);
  not not_8 (not_8_out, Z);
  not not_9 (not_9_out, X);
  not not_10 (not_10_out, Y);
  and and_1 (and_1_out, not_1_out, Y, Z);
  and and_2 (and_2_out, X, not_2_out, Z);
  and and_3 (and_3_out, not_3_out, Y, Z);
  and and_4 (and_4_out, X, not_4_out);
  and and_5 (and_5_out, not_5_out, not_6_out, Z);
  and and_6 (and_6_out, not_7_out, Y, not_8_out);
  and and_7 (and_7_out, not_9_out, Y, Z);
  and and_8 (and_8_out, X, not_10_out, Z);
  or or_1 (Cin, and_1_out, and_2_out);
  or or_2 (OP1, and_3_out, and_4_out);
  or or_3 (OP0, and_5_out, and_6_out);
  or or_4 (Comp, and_7_out, and_8_out);
endmodule

module ALU_8_bits_completa_uso (
  input  [2:0] Operacion,
  input  [7:0] A,
  input  [7:0] B,
  output [7:0] Salida,
  output Desborde
);

  ALU_8_bits_completa alu_8_bits_completa_1 (.Op(Operacion), .Salida(Salida), .A(A), .B(B), .C_out(Desborde));
endmodule
