// Logisim project Practica03.circ as structural Verilog: 15 circuits, main circuit 0-9
module Funcion_0_9 (
  input  X,
  input  Y,
  input  W,
  input  Z,
  output A,
  output B,
  output C,
  output D
);

  wire and_1_out, and_2_out, and_3_out, and_4_out, and_5_out, and_6_out, and_7_out, and_8_out, and_9_out,
       not_1_out, not_2_out, not_3_out, not_4_out, not_5_out, not_6_out, not_7_out, not_8_out, not_9_out,
       not_10_out, not_11_out, not_12_out, not_13_out, not_14_out, not_15_out, not_16_out, not_17_out,
       not_18_out, not_19_out;

  not not_1 (not_1_out, X);
  not not_2 (not_2_out, Y);
  not not_3 (not_3_out, W);
  not not_4 (not_4_out, Z);
  not not_5 (not_5_out, X);
  not not_6 (not_6_out, Y);
  not not_7 (not_7_out, X);
  not not_8 (not_8_out, W);
  not not_9 (not_9_out, X);
  not not_10 (not_10_out, Z);
  not not_11 (not_11_out, X);
  and and_1 (and_1_out, not_11_out, not_12_out, Z);
  not not_12 (not_12_out, W);
  not not_13 (not_13_out, X);
  and and_2 (and_2_out, not_13_out, W, not_14_out);
  not not_14 (not_14_out, Z);
  not not_15 (not_15_out, X);
  and and_3 (and_3_out, not_15_out, not_16_out);
  not not_16 (not_16_out, Z);
  not not_17 (not_17_out, Y);
  not not_18 (not_18_out, W);
  and and_4 (and_4_out, not_17_out, not_18_out, not_19_out);
  not not_19 (not_19_out, Z);
  and and_5 (and_5_out, not_1_out, Y, W, Z);
  or or_1 (A, and_5_out, and_6_out);
  and and_6 (and_6_out, X, not_2_out, not_3_out, not_4_out);
  and and_7 (and_7_out, not_5_out, not_6_out, W, Z);
  and and_8 (and_8_out, not_7_out, Y, not_8_out);
  or or_2 (B, and_7_out, and_8_out, and_9_out);
  and and_9 (and_9_out, not_9_out, Y, not_10_out);
  or or_3 (C, and_1_out, and_2_out);
  or or_4 (D, and_3_out, and_4_out);
endmodule

module Controla_J_K (
  input  X,
  input  Y,
  input  W,
  input  Z,
  output J1,
  output K1,
  output J2,
  output K2,
  output J3,
  output K3,
  output J4,
  output K4
);

  wire and_3_out, and_4_out, and_5_out, and_6_out, and_7_out, and_8_out, not_1_out, not_2_out, not_3_out,
       not_4_out, not_5_out, not_6_out, not_7_out, not_8_out, not_9_out, not_10_out, not_11_out, not_12_out,
       not_13_out, not_14_out, not_15_out, not_16_out, not_17_out, not_18_out, not_19_out, not_20_out,
       not_21_out, not_22_out, not_23_out, not_24_out, not_25_out, not_26_out, not_27_out, not_28_out,
       not_29_out;

  not not_1 (not_1_out, Y);
  not not_2 (not_2_out, W);
  not not_3 (not_3_out, Z);
  not not_4 (not_4_out, X);
  not not_5 (not_5_out, Y);
  not not_6 (not_6_out, W);
  not not_7 (not_7_out, Z);
  not not_8 (not_8_out, X);
  not not_9 (not_9_out, W);
  not not_10 (not_10_out, Z);
  not not_11 (not_11_out, Y);
  not not_12 (not_12_out, W);
  and and_1 (K2, not_11_out, not_12_out, not_13_out);
  not not_13 (not_13_out, Z);
  not not_14 (not_14_out, X);
  and and_2 (J3, not_14_out, W, not_15_out);
  not not_15 (not_15_out, Z);
  not not_16 (not_16_out, X);
  and and_3 (and_3_out, not_16_out, not_17_out, not_18_out);
  not not_17 (not_17_out, W);
  not not_18 (not_18_out, Z);
  not not_19 (not_19_out, Y);
  and and_4 (and_4_out, not_19_out, not_20_out, not_21_out);
  not not_20 (not_20_out, W);
  not not_21 (not_21_out, Z);
  not not_22 (not_22_out, X);
  and and_5 (and_5_out, not_22_out, Z);
  not not_23 (not_23_out, Y);
  and and_6 (and_6_out, not_23_out, not_24_out, Z);
  not not_24 (not_24_out, W);
  not not_25 (not_25_out, X);
  and and_7 (and_7_out, not_25_out, not_26_out);
  not not_26 (not_26_out, Z);
  not not_27 (not_27_out, Y);
  and and_8 (and_8_out, not_27_out, not_28_out, not_29_out);
  not not_28 (not_28_out, W);
  not not_29 (not_29_out, Z);
  and and_9 (J1, X, not_1_out, not_2_out, not_3_out);
  and and_10 (K1, not_4_out, not_5_out, not_6_out, not_7_out);
  and and_11 (J2, not_8_out, Y, not_9_out, not_10_out);
  or or_1 (K3, and_3_out, and_4_out);
  or or_2 (J4, and_5_out, and_6_out);
  or or_3 (K4, and_7_out, and_8_out);
endmodule

module Control_Display (
  input  X,
  input  Y,
  input  W,
  input  Z,
  output A,
  output B,
  output C,
  output D,
  output E,
  output F,
  output G,
  output H
);

  wire and_1_out, and_2_out, and_3_out, and_4_out, and_5_out, and_6_out, and_7_out, and_8_out, and_9_out,
       and_10_out, and_11_out, and_12_out, and_13_out, and_14_out, and_15_out, and_16_out, and_17_out,
       and_18_out, and_19_out, and_20_out, and_21_out, and_22_out, and_23_out, and_24_out, and_25_out,
       not_1_out, not_2_out, not_3_out, not_4_out, not_5_out, not_6_out, not_7_out, not_8_out, not_9_out,
       not_10_out, not_11_out, not_12_out, not_13_out, not_14_out, not_15_out, not_16_out, not_17_out,
       not_18_out, not_19_out, not_20_out, not_21_out, not_22_out, not_23_out, not_24_out, not_25_out,
       not_26_out, not_27_out, not_28_out, not_29_out, not_30_out, not_31_out, not_32_out, not_33_out,
       not_34_out, not_35_out, not_36_out, not_37_out, not_38_out, not_39_out, not_40_out, not_41_out,
       not_42_out, not_43_out, not_44_out, not_45_out, not_46_out, not_47_out, not_48_out, not_49_out,
       not_50_out;

  not not_1 (not_1_out, X);
  and and_1 (and_1_out, not_1_out, not_2_out, W);
  not not_2 (not_2_out, Y);
  not not_3 (not_3_out, X);
  and and_2 (and_2_out, not_3_out, Y, not_4_out);
  not not_4 (not_4_out, W);
  not not_5 (not_5_out, X);
  and and_3 (and_3_out, not_5_out, Y, not_6_out);
  not not_6 (not_6_out, Z);
  not not_7 (not_7_out, Y);
  and and_4 (and_4_out, X, not_7_out, not_8_out);
  not not_8 (not_8_out, W);
  not not_9 (not_9_out, X);
  and and_5 (and_5_out, not_9_out, not_10_out, not_11_out);
  not not_10 (not_10_out, W);
  not not_11 (not_11_out, Z);
  not not_12 (not_12_out, X);
  and and_6 (and_6_out, not_12_out, Y, not_13_out);
  not not_13 (not_13_out, W);
  not not_14 (not_14_out, X);
  and and_7 (and_7_out, not_14_out, Y, not_15_out);
  not not_15 (not_15_out, Z);
  not not_16 (not_16_out, Y);
  and and_8 (and_8_out, X, not_16_out, not_17_out);
  not not_17 (not_17_out, W);
  not not_18 (not_18_out, X);
  and and_9 (and_9_out, not_18_out, not_19_out, not_20_out);
  not not_19 (not_19_out, Y);
  not not_20 (not_20_out, Z);
  not not_21 (not_21_out, X);
  and and_10 (and_10_out, not_21_out, W);
  not not_22 (not_22_out, X);
  and and_11 (and_11_out, not_22_out, Y, Z);
  not not_23 (not_23_out, Y);
  and and_12 (and_12_out, X, not_23_out, not_24_out);
  not not_24 (not_24_out, W);
  not not_25 (not_25_out, X);
  and and_13 (and_13_out, not_25_out, not_26_out);
  not not_26 (not_26_out, Y);
  not not_27 (not_27_out, X);
  and and_14 (and_14_out, not_27_out, not_28_out, not_29_out);
  not not_28 (not_28_out, W);
  not not_29 (not_29_out, Z);
  not not_30 (not_30_out, Y);
  and and_15 (and_15_out, not_30_out, not_31_out);
  not not_31 (not_31_out, W);
  not not_32 (not_32_out, X);
  and and_16 (and_16_out, not_32_out, W, Z);
  not not_33 (not_33_out, Y);
  not not_34 (not_34_out, W);
  and and_17 (and_17_out, not_33_out, not_34_out, not_35_out);
  not not_35 (not_35_out, Z);
  not not_36 (not_36_out, X);
  and and_18 (and_18_out, not_36_out, W, not_37_out);
  not not_37 (not_37_out, Z);
  not not_38 (not_38_out, Y);
  not not_39 (not_39_out, W);
  not not_40 (not_40_out, Z);
  not not_41 (not_41_out, X);
  not not_42 (not_42_out, Y);
  not not_43 (not_43_out, X);
  not not_44 (not_44_out, Z);
  not not_45 (not_45_out, X);
  not not_46 (not_46_out, W);
  not not_47 (not_47_out, Y);
  and and_19 (and_19_out, not_47_out, not_48_out);
  not not_48 (not_48_out, W);
  not not_49 (not_49_out, X);
  and and_20 (and_20_out, not_49_out, Z);
  not not_50 (not_50_out, X);
  and and_21 (and_21_out, not_50_out, Y);
  or or_1 (A, and_1_out, and_2_out, and_3_out, and_4_out);
  or or_2 (B, and_5_out, and_6_out, and_7_out, and_8_out);
  or or_3 (C, and_9_out, and_10_out, and_11_out, and_12_out);
  or or_4 (D, and_13_out, and_14_out, and_15_out, and_16_out);
  or or_5 (E, and_17_out, and_18_out);
  and and_22 (and_22_out, not_38_out, not_39_out, not_40_out);
  and and_23 (and_23_out, not_41_out, not_42_out, W);
  and and_24 (and_24_out, not_43_out, W, not_44_out);
  and and_25 (and_25_out, not_45_out, Y, not_46_out, Z);
  or or_6 (G, and_19_out, and_20_out, and_21_out);
  or or_7 (F, and_22_out, and_23_out, and_24_out, and_25_out);

  assign H = 1'b0;
endmodule

module Controlador_999 (
  input  X,
  input  Y,
  input  W,
  input  Z,
  input  AND,
  output J1,
  output K1,
  output J2,
  output k2,
  output J3,
  output k3,
  output J4,
  output K4
);

  wire and_4_out, and_5_out, and_7_out, and_8_out, and_9_out, and_10_out, and_11_out, and_12_out, and_13_out,
       not_1_out, not_2_out, not_3_out, not_4_out, not_5_out, not_6_out, not_7_out, not_8_out, not_9_out,
       not_10_out, not_11_out, not_12_out, not_13_out, not_14_out, not_15_out, not_16_out, not_17_out,
       not_18_out, not_19_out, not_20_out, not_21_out, not_22_out, not_23_out, not_24_out, not_25_out;

  not not_1 (not_1_out, Y);
  not not_2 (not_2_out, W);
  not not_3 (not_3_out, X);
  not not_4 (not_4_out, X);
  not not_5 (not_5_out, Y);
  not not_6 (not_6_out, W);
  not not_7 (not_7_out, Z);
  not not_8 (not_8_out, Y);
  not not_9 (not_9_out, W);
  not not_10 (not_10_out, X);
  not not_11 (not_11_out, Y);
  not not_12 (not_12_out, W);
  not not_13 (not_13_out, Z);
  not not_14 (not_14_out, X);
  not not_15 (not_15_out, W);
  not not_16 (not_16_out, Y);
  not not_17 (not_17_out, W);
  not not_18 (not_18_out, X);
  not not_19 (not_19_out, Y);
  not not_20 (not_20_out, W);
  not not_21 (not_21_out, X);
  not not_22 (not_22_out, Z);
  not not_23 (not_23_out, Y);
  not not_24 (not_24_out, W);
  not not_25 (not_25_out, Z);
  and and_1 (J1, X, not_1_out, not_2_out, AND);
  and and_2 (K1, not_3_out, AND);
  and and_3 (J2, not_4_out, Y, AND);
  and and_4 (and_4_out, not_5_out, not_6_out, not_7_out, AND);
  and and_5 (and_5_out, X, not_8_out, not_9_out, AND);
  and and_6 (J3, not_10_out, W, AND);
  and and_7 (and_7_out, not_11_out, not_12_out, not_13_out, AND);
  and and_8 (and_8_out, not_14_out, Y, not_15_out, AND);
  and and_9 (and_9_out, X, not_16_out, not_17_out, AND);
  and and_10 (and_10_out, not_18_out, Z, AND);
  and and_11 (and_11_out, not_19_out, not_20_out, Z, AND);
  and and_12 (and_12_out, not_21_out, not_22_out, AND);
  and and_13 (and_13_out, not_23_out, not_24_out, not_25_out, AND);
  or or_1 (k2, and_4_out, and_5_out);
  or or_2 (k3, and_7_out, and_8_out, and_9_out);
  or or_3 (J4, and_10_out, and_11_out);
  or or_4 (K4, and_12_out, and_13_out);
endmodule

module Funcion_Automata (
  input  Estado1,
  input  Estado2,
  input  Entrada,
  output Estado1_2,
  output Estado2_2
);

  wire and_1_out, and_2_out, and_3_out, not_1_out, not_2_out, not_3_out, not_4_out, not_5_out;

  not not_1 (not_1_out, Estado1);
  not not_2 (not_2_out, Entrada);
  not not_3 (not_3_out, Estado2);
  not not_4 (not_4_out, Estado2);
  not not_5 (not_5_out, Entrada);
  and and_1 (and_1_out, not_1_out, Estado2, not_2_out);
  and and_2 (and_2_out, Estado1, not_3_out);
  and and_3 (and_3_out, Estado1, Entrada);
  and and_4 (Estado2_2, not_4_out, not_5_out);
  or or_1 (Estado1_2, and_1_out, and_2_out, and_3_out);
endmodule

module Controlador_Registro (
  input  Entrada,
  input  Q,
  output S,
  output R
);

  wire not_1_out, not_2_out;

  not not_1 (not_1_out, Q);
  not not_2 (not_2_out, Entrada);
  and and_1 (S, Entrada, not_1_out);
  and and_2 (R, not_2_out, Q);
endmodule

module Control_Registro (
  input  Escribir,
  input  EscrbirRegistro1,
  input  EscribirRegistro0,
  output R1,
  output R2,
  output R3,
  output R4
);

  wire not_1_out, not_2_out, not_3_out, not_4_out;

  not not_1 (not_1_out, EscrbirRegistro1);
  not not_2 (not_2_out, EscribirRegistro0);
  not not_3 (not_3_out, EscrbirRegistro1);
  not not_4 (not_4_out, EscribirRegistro0);
  and and_1 (R4, Escribir, EscrbirRegistro1, EscribirRegistro0);
  and and_2 (R1, Escribir, not_1_out, not_2_out);
  and and_3 (R2, Escribir, not_3_out, EscribirRegistro0);
  and and_4 (R3, Escribir, EscrbirRegistro1, not_4_out);
endmodule

module _0_9 (
);

  wire clock_1_out, controla_j_k_1_j1, controla_j_k_1_j2, controla_j_k_1_j3, controla_j_k_1_j4,
       controla_j_k_1_k1, controla_j_k_1_k2, controla_j_k_1_k3, controla_j_k_1_k4, funcion_0_9_1_a,
       funcion_0_9_1_b, funcion_0_9_1_c, funcion_0_9_1_d, j_k_ff_1_q, j_k_ff_2_q, j_k_ff_3_q, j_k_ff_4_q;

  Controla_J_K controla_j_k_1 (
    .X(funcion_0_9_1_a), .Y(funcion_0_9_1_b), .W(funcion_0_9_1_c), .Z(funcion_0_9_1_d),
    .J1(controla_j_k_1_j1), .K1(controla_j_k_1_k1), .J2(controla_j_k_1_j2), .K2(controla_j_k_1_k2),
    .J3(controla_j_k_1_j3), .K3(controla_j_k_1_k3), .J4(controla_j_k_1_j4), .K4(controla_j_k_1_k4));
  Funcion_0_9 funcion_0_9_1 (
    .X(j_k_ff_1_q), .Y(j_k_ff_2_q), .W(j_k_ff_3_q), .Z(j_k_ff_4_q), .A(funcion_0_9_1_a), .B(funcion_0_9_1_b),
    .C(funcion_0_9_1_c), .D(funcion_0_9_1_d));
  Clock clock_1 (.out(clock_1_out));
  J_K_Flip_Flop j_k_ff_1 (
    .J(controla_j_k_1_j1), .clk(clock_1_out), .K(controla_j_k_1_k1), .Q(j_k_ff_1_q));  // open: Qn, preset, en, reset
  J_K_Flip_Flop j_k_ff_2 (
    .J(controla_j_k_1_j2), .clk(clock_1_out), .K(controla_j_k_1_k2), .Q(j_k_ff_2_q));  // open: Qn, preset, en, reset
  J_K_Flip_Flop j_k_ff_3 (
    .J(controla_j_k_1_j3), .clk(clock_1_out), .K(controla_j_k_1_k3), .Q(j_k_ff_3_q));  // open: Qn, preset, en, reset
  J_K_Flip_Flop j_k_ff_4 (
    .J(controla_j_k_1_j4), .clk(clock_1_out), .K(controla_j_k_1_k4), .Q(j_k_ff_4_q));  // open: Qn, preset, en, reset
endmodule

module _0___9_Display (
);

  wire clock_1_out, control_display_1_a, control_display_1_b, control_display_1_c, control_display_1_d,
       control_display_1_e, control_display_1_f, control_display_1_g, control_display_1_h, controla_j_k_1_j1,
       controla_j_k_1_j2, controla_j_k_1_j3, controla_j_k_1_j4, controla_j_k_1_k1, controla_j_k_1_k2,
       controla_j_k_1_k3, controla_j_k_1_k4, funcion_0_9_1_a, funcion_0_9_1_b, funcion_0_9_1_c,
       funcion_0_9_1_d, j_k_ff_1_q, j_k_ff_2_q, j_k_ff_3_q, j_k_ff_4_q;

  Funcion_0_9 funcion_0_9_1 (
    .X(j_k_ff_1_q), .Y(j_k_ff_2_q), .W(j_k_ff_3_q), .Z(j_k_ff_4_q), .A(funcion_0_9_1_a), .B(funcion_0_9_1_b),
    .C(funcion_0_9_1_c), .D(funcion_0_9_1_d));
  Controla_J_K controla_j_k_1 (
    .X(funcion_0_9_1_a), .Y(funcion_0_9_1_b), .W(funcion_0_9_1_c), .Z(funcion_0_9_1_d),
    .J1(controla_j_k_1_j1), .K1(controla_j_k_1_k1), .J2(controla_j_k_1_j2), .K2(controla_j_k_1_k2),
    .J3(controla_j_k_1_j3), .K3(controla_j_k_1_k3), .J4(controla_j_k_1_j4), .K4(controla_j_k_1_k4));
  Clock clock_1 (.out(clock_1_out));
  J_K_Flip_Flop j_k_ff_1 (
    .J(controla_j_k_1_j1), .clk(clock_1_out), .K(controla_j_k_1_k1), .Q(j_k_ff_1_q));  // open: Qn, preset, en, reset
  J_K_Flip_Flop j_k_ff_2 (
    .J(controla_j_k_1_j2), .clk(clock_1_out), .K(controla_j_k_1_k2), .Q(j_k_ff_2_q));  // open: Qn, preset, en, reset
  J_K_Flip_Flop j_k_ff_3 (
    .J(controla_j_k_1_j3), .clk(clock_1_out), .K(controla_j_k_1_k3), .Q(j_k_ff_3_q));  // open: Qn, preset, en, reset
  J_K_Flip_Flop j_k_ff_4 (
    .J(controla_j_k_1_j4), .clk(clock_1_out), .K(controla_j_k_1_k4), .Q(j_k_ff_4_q));  // open: Qn, preset, en, reset
  Control_Display control_display_1 (
    .X(j_k_ff_1_q), .Y(j_k_ff_2_q), .W(j_k_ff_3_q), .Z(j_k_ff_4_q), .A(control_display_1_a),
    .B(control_display_1_b), .C(control_display_1_c), .D(control_display_1_d), .E(control_display_1_e),
    .F(control_display_1_f), .G(control_display_1_g), .H(control_display_1_h));
  _7_Segment_Display u_7_segment_display_1 (
    .g(control_display_1_a), .f(control_display_1_b), .a(control_display_1_c), .b(control_display_1_d),
    .e(control_display_1_e), .d(control_display_1_f), .c(control_display_1_g), .dp(control_display_1_h));
endmodule

module _0_999_Display (
);

  wire and_1_out, and_2_out, clock_1_out, control_display_1_a, control_display_1_b, control_display_1_c,
       control_display_1_d, control_display_1_e, control_display_1_f, control_display_1_g,
       control_display_1_h, control_display_2_a, control_display_2_b, control_display_2_c,
       control_display_2_d, control_display_2_e, control_display_2_f, control_display_2_g,
       control_display_2_h, control_display_3_a, control_display_3_b, control_display_3_c,
       control_display_3_d, control_display_3_e, control_display_3_f, control_display_3_g,
       control_display_3_h, controla_j_k_1_j1, controla_j_k_1_j2, controla_j_k_1_j3, controla_j_k_1_j4,
       controla_j_k_1_k1, controla_j_k_1_k2, controla_j_k_1_k3, controla_j_k_1_k4, controlador_999_1_j1,
       controlador_999_1_j2, controlador_999_1_j3, controlador_999_1_j4, controlador_999_1_k1,
       controlador_999_1_k2, controlador_999_1_k3, controlador_999_1_k4, controlador_999_2_j1,
       controlador_999_2_j2, controlador_999_2_j3, controlador_999_2_j4, controlador_999_2_k1,
       controlador_999_2_k2, controlador_999_2_k3, controlador_999_2_k4, funcion_0_9_1_a, funcion_0_9_1_b,
       funcion_0_9_1_c, funcion_0_9_1_d, funcion_0_9_2_a, funcion_0_9_2_b, funcion_0_9_2_c, funcion_0_9_2_d,
       funcion_0_9_3_a, funcion_0_9_3_b, funcion_0_9_3_c, funcion_0_9_3_d, j_k_ff_1_q, j_k_ff_2_q,
       j_k_ff_3_q, j_k_ff_4_q, j_k_ff_5_q, j_k_ff_6_q, j_k_ff_7_q, j_k_ff_8_q, j_k_ff_9_q, j_k_ff_10_q,
       j_k_ff_11_q, j_k_ff_12_q;

  Funcion_0_9 funcion_0_9_1 (
    .X(j_k_ff_1_q), .Y(j_k_ff_2_q), .W(j_k_ff_3_q), .Z(j_k_ff_4_q), .A(funcion_0_9_1_a), .B(funcion_0_9_1_b),
    .C(funcion_0_9_1_c), .D(funcion_0_9_1_d));
  Funcion_0_9 funcion_0_9_2 (
    .X(j_k_ff_5_q), .Y(j_k_ff_6_q), .W(j_k_ff_7_q), .Z(j_k_ff_8_q), .A(funcion_0_9_2_a), .B(funcion_0_9_2_b),
    .C(funcion_0_9_2_c), .D(funcion_0_9_2_d));
  Funcion_0_9 funcion_0_9_3 (
    .X(j_k_ff_9_q), .Y(j_k_ff_10_q), .W(j_k_ff_11_q), .Z(j_k_ff_12_q), .A(funcion_0_9_3_a),
    .B(funcion_0_9_3_b), .C(funcion_0_9_3_c), .D(funcion_0_9_3_d));
  Controla_J_K controla_j_k_1 (
    .X(funcion_0_9_1_a), .Y(funcion_0_9_1_b), .W(funcion_0_9_1_c), .Z(funcion_0_9_1_d),
    .J1(controla_j_k_1_j1), .K1(controla_j_k_1_k1), .J2(controla_j_k_1_j2), .K2(controla_j_k_1_k2),
    .J3(controla_j_k_1_j3), .K3(controla_j_k_1_k3), .J4(controla_j_k_1_j4), .K4(controla_j_k_1_k4));
  Clock clock_1 (.out(clock_1_out));
  Controlador_999 controlador_999_1 (
    .X(funcion_0_9_2_a), .Y(funcion_0_9_2_b), .W(funcion_0_9_2_c), .Z(funcion_0_9_2_d), .AND(and_1_out),
    .J1(controlador_999_1_j1), .K1(controlador_999_1_k1), .J2(controlador_999_1_j2),
    .k2(controlador_999_1_k2), .J3(controlador_999_1_j3), .k3(controlador_999_1_k3),
    .J4(controlador_999_1_j4), .K4(controlador_999_1_k4));
  Controlador_999 controlador_999_2 (
    .X(funcion_0_9_3_a), .Y(funcion_0_9_3_b), .W(funcion_0_9_3_c), .Z(funcion_0_9_3_d), .AND(and_2_out),
    .J1(controlador_999_2_j1), .K1(controlador_999_2_k1), .J2(controlador_999_2_j2),
    .k2(controlador_999_2_k2), .J3(controlador_999_2_j3), .k3(controlador_999_2_k3),
    .J4(controlador_999_2_j4), .K4(controlador_999_2_k4));
  J_K_Flip_Flop j_k_ff_1 (
    .J(controla_j_k_1_j1), .clk(clock_1_out), .K(controla_j_k_1_k1), .Q(j_k_ff_1_q));  // open: Qn, preset, en, reset
  J_K_Flip_Flop j_k_ff_2 (
    .J(controla_j_k_1_j2), .clk(clock_1_out), .K(controla_j_k_1_k2), .Q(j_k_ff_2_q));  // open: Qn, preset, en, reset
  J_K_Flip_Flop j_k_ff_3 (
    .J(controla_j_k_1_j3), .clk(clock_1_out), .K(controla_j_k_1_k3), .Q(j_k_ff_3_q));  // open: Qn, preset, en, reset
  J_K_Flip_Flop j_k_ff_4 (
    .J(controla_j_k_1_j4), .clk(clock_1_out), .K(controla_j_k_1_k4), .Q(j_k_ff_4_q));  // open: Qn, preset, en, reset
  J_K_Flip_Flop j_k_ff_5 (
    .J(controlador_999_1_j1), .clk(clock_1_out), .K(controlador_999_1_k1), .Q(j_k_ff_5_q));  // open: Qn, preset, en, reset
  J_K_Flip_Flop j_k_ff_6 (
    .J(controlador_999_1_j2), .clk(clock_1_out), .K(controlador_999_1_k2), .Q(j_k_ff_6_q));  // open: Qn, preset, en, reset
  J_K_Flip_Flop j_k_ff_7 (
    .J(controlador_999_1_j3), .clk(clock_1_out), .K(controlador_999_1_k3), .Q(j_k_ff_7_q));  // open: Qn, preset, en, reset
  J_K_Flip_Flop j_k_ff_8 (
    .J(controlador_999_1_j4), .clk(clock_1_out), .K(controlador_999_1_k4), .Q(j_k_ff_8_q));  // open: Qn, preset, en, reset
  J_K_Flip_Flop j_k_ff_9 (
    .J(controlador_999_2_j1), .clk(clock_1_out), .K(controlador_999_2_k1), .Q(j_k_ff_9_q));  // open: Qn, preset, en, reset
  J_K_Flip_Flop j_k_ff_10 (
    .J(controlador_999_2_j2), .clk(clock_1_out), .K(controlador_999_2_k2), .Q(j_k_ff_10_q));  // open: Qn, preset, en, reset
  J_K_Flip_Flop j_k_ff_11 (
    .J(controlador_999_2_j3), .clk(clock_1_out), .K(controlador_999_2_k3), .Q(j_k_ff_11_q));  // open: Qn, preset, en, reset
  J_K_Flip_Flop j_k_ff_12 (
    .J(controlador_999_2_j4), .clk(clock_1_out), .K(controlador_999_2_k4), .Q(j_k_ff_12_q));  // open: Qn, preset, en, reset
  and and_1 (and_1_out, j_k_ff_1_q, ~j_k_ff_2_q, ~j_k_ff_3_q, j_k_ff_4_q);  // AND_Gate
  and and_2 (and_2_out, j_k_ff_5_q, ~j_k_ff_6_q, ~j_k_ff_7_q, j_k_ff_8_q, and_1_out);  // AND_Gate
  Control_Display control_display_1 (
    .X(j_k_ff_9_q), .Y(j_k_ff_10_q), .W(j_k_ff_11_q), .Z(j_k_ff_12_q), .A(control_display_1_a),
    .B(control_display_1_b), .C(control_display_1_c), .D(control_display_1_d), .E(control_display_1_e),
    .F(control_display_1_f), .G(control_display_1_g), .H(control_display_1_h));
  _7_Segment_Display u_7_segment_display_1 (
    .g(control_display_1_a), .f(control_display_1_b), .a(control_display_1_c), .b(control_display_1_d),
    .e(control_display_1_e), .d(control_display_1_f), .c(control_display_1_g), .dp(control_display_1_h));
  Control_Display control_display_2 (
    .X(j_k_ff_5_q), .Y(j_k_ff_6_q), .W(j_k_ff_7_q), .Z(j_k_ff_8_q), .A(control_display_2_a),
    .B(control_display_2_b), .C(control_display_2_c), .D(control_display_2_d), .E(control_display_2_e),
    .F(control_display_2_f), .G(control_display_2_g), .H(control_display_2_h));
  _7_Segment_Display u_7_segment_display_2 (
    .g(control_display_2_a), .f(control_display_2_b), .a(control_display_2_c), .b(control_display_2_d),
    .e(control_display_2_e), .d(control_display_2_f), .c(control_display_2_g), .dp(control_display_2_h));
  Control_Display control_display_3 (
    .X(j_k_ff_1_q), .Y(j_k_ff_2_q), .W(j_k_ff_3_q), .Z(j_k_ff_4_q), .A(control_display_3_a),
    .B(control_display_3_b), .C(control_display_3_c), .D(control_display_3_d), .E(control_display_3_e),
    .F(control_display_3_f), .G(control_display_3_g), .H(control_display_3_h));
  _7_Segment_Display u_7_segment_display_3 (
    .g(control_display_3_a), .f(control_display_3_b), .a(control_display_3_c), .b(control_display_3_d),
    .e(control_display_3_e), .d(control_display_3_f), .c(control_display_3_g), .dp(control_display_3_h));
endmodule

module Automata (
  input  Entrada,
  output out_2,
  output out_3
);

  wire clock_1_out, funcion_automata_1_estado1_2, funcion_automata_1_estado2_2;

  Funcion_Automata funcion_automata_1 (
    .Estado1(out_2), .Estado2(out_3), .Entrada(Entrada), .Estado1_2(funcion_automata_1_estado1_2),
    .Estado2_2(funcion_automata_1_estado2_2));
  Clock clock_1 (.out(clock_1_out));
  D_Flip_Flop d_ff_1 (.clk(clock_1_out), .D(funcion_automata_1_estado1_2), .Q(out_2));  // open: Qn, preset, en, reset
  D_Flip_Flop d_ff_2 (.clk(clock_1_out), .D(funcion_automata_1_estado2_2), .Q(out_3));  // open: Qn, preset, en, reset

  // Notes on the sheet:
  //   Estado   --   Representacion
  //   T   --  00
  //   TE   --   01
  //   NT   --   10
  //   NTE   --   11
  //   Entrada   --   Representa
  //   0   --   Error
  //   1   --   Acierto
endmodule

module Registro (
  input  Reloj,
  input  Escribe,
  input  [7:0] Escribir,
  output [7:0] Lectura
);

  wire controlador_registro_1_r, controlador_registro_1_s, controlador_registro_2_r,
       controlador_registro_2_s, controlador_registro_3_r, controlador_registro_3_s,
       controlador_registro_4_r, controlador_registro_4_s, controlador_registro_5_r,
       controlador_registro_5_s, controlador_registro_6_r, controlador_registro_6_s,
       controlador_registro_7_r, controlador_registro_7_s, controlador_registro_8_r,
       controlador_registro_8_s, multiplexer_1_out;

  Multiplexer #(.enable("false")) multiplexer_1 (.in0(1'b0), .in1(Reloj), .out(multiplexer_1_out), .sel(Escribe));
  Controlador_Registro controlador_registro_1 (
    .Entrada(Escribir[7]), .Q(Lectura[7]), .S(controlador_registro_1_s), .R(controlador_registro_1_r));
  S_R_Flip_Flop s_r_ff_1 (
    .S(controlador_registro_1_s), .clk(multiplexer_1_out), .R(controlador_registro_1_r), .Q(Lectura[7]));  // open: Qn, preset, reset, en
  Controlador_Registro controlador_registro_2 (
    .Entrada(Escribir[6]), .Q(Lectura[6]), .S(controlador_registro_2_s), .R(controlador_registro_2_r));
  S_R_Flip_Flop s_r_ff_2 (
    .S(controlador_registro_2_s), .clk(multiplexer_1_out), .R(controlador_registro_2_r), .Q(Lectura[6]));  // open: Qn, preset, reset, en
  S_R_Flip_Flop s_r_ff_3 (
    .S(controlador_registro_3_s), .clk(multiplexer_1_out), .R(controlador_registro_3_r), .Q(Lectura[5]));  // open: Qn, preset, reset, en
  Controlador_Registro controlador_registro_3 (
    .Entrada(Escribir[5]), .Q(Lectura[5]), .S(controlador_registro_3_s), .R(controlador_registro_3_r));
  S_R_Flip_Flop s_r_ff_4 (
    .S(controlador_registro_4_s), .clk(multiplexer_1_out), .R(controlador_registro_4_r), .Q(Lectura[4]));  // open: Qn, preset, reset, en
  Controlador_Registro controlador_registro_4 (
    .Entrada(Escribir[4]), .Q(Lectura[4]), .S(controlador_registro_4_s), .R(controlador_registro_4_r));
  S_R_Flip_Flop s_r_ff_5 (
    .S(controlador_registro_5_s), .clk(multiplexer_1_out), .R(controlador_registro_5_r), .Q(Lectura[3]));  // open: Qn, preset, reset, en
  Controlador_Registro controlador_registro_5 (
    .Entrada(Escribir[3]), .Q(Lectura[3]), .S(controlador_registro_5_s), .R(controlador_registro_5_r));
  S_R_Flip_Flop s_r_ff_6 (
    .S(controlador_registro_6_s), .clk(multiplexer_1_out), .R(controlador_registro_6_r), .Q(Lectura[2]));  // open: Qn, preset, reset, en
  Controlador_Registro controlador_registro_6 (
    .Entrada(Escribir[2]), .Q(Lectura[2]), .S(controlador_registro_6_s), .R(controlador_registro_6_r));
  S_R_Flip_Flop s_r_ff_7 (
    .S(controlador_registro_7_s), .clk(multiplexer_1_out), .R(controlador_registro_7_r), .Q(Lectura[1]));  // open: Qn, preset, reset, en
  Controlador_Registro controlador_registro_7 (
    .Entrada(Escribir[1]), .Q(Lectura[1]), .S(controlador_registro_7_s), .R(controlador_registro_7_r));
  S_R_Flip_Flop s_r_ff_8 (
    .S(controlador_registro_8_s), .clk(multiplexer_1_out), .R(controlador_registro_8_r), .Q(Lectura[0]));  // open: Qn, preset, reset, en
  Controlador_Registro controlador_registro_8 (
    .Entrada(Escribir[0]), .Q(Lectura[0]), .S(controlador_registro_8_s), .R(controlador_registro_8_r));
endmodule

module Banco_de_Registros (
  input  Reloj,
  input  [1:0] Leer_Registro_1,
  input  [1:0] Leer_Registro_2,
  input  [7:0] Escribir_Datos,
  input  Escribir,
  input  [1:0] Escribir_Registro,
  output [7:0] Leer_Datos_1,
  output [7:0] Leer_Datos_2
);

  wire control_registro_1_r1, control_registro_1_r2, control_registro_1_r3, control_registro_1_r4;
  wire [7:0] demultiplexer_1_out0, demultiplexer_1_out1, demultiplexer_1_out2, demultiplexer_1_out3,
       registro_1_lectura, registro_2_lectura, registro_3_lectura, registro_4_lectura;

  Control_Registro control_registro_1 (
    .Escribir(Escribir), .EscrbirRegistro1(Escribir_Registro[1]), .EscribirRegistro0(Escribir_Registro[0]),
    .R1(control_registro_1_r1), .R2(control_registro_1_r2), .R3(control_registro_1_r3),
    .R4(control_registro_1_r4));
  Registro registro_1 (
    .Lectura(registro_1_lectura), .Escribe(control_registro_1_r1), .Escribir(demultiplexer_1_out0),
    .Reloj(Reloj));
  Demultiplexer #(.select(2), .width(8)) demultiplexer_1 (
    .out0(demultiplexer_1_out0), .out1(demultiplexer_1_out1), .out2(demultiplexer_1_out2),
    .out3(demultiplexer_1_out3), .in(Escribir_Datos), .sel(Escribir_Registro), .en(Escribir));
  Registro registro_2 (
    .Lectura(registro_2_lectura), .Escribe(control_registro_1_r2), .Escribir(demultiplexer_1_out1),
    .Reloj(Reloj));
  Registro registro_3 (
    .Lectura(registro_3_lectura), .Escribe(control_registro_1_r3), .Escribir(demultiplexer_1_out2),
    .Reloj(Reloj));
  Registro registro_4 (
    .Lectura(registro_4_lectura), .Escribe(control_registro_1_r4), .Escribir(demultiplexer_1_out3),
    .Reloj(Reloj));
  Multiplexer #(.select(2), .width(8), .enable("false")) multiplexer_1 (
    .in0(registro_1_lectura), .in1(registro_2_lectura), .in2(registro_3_lectura), .in3(registro_4_lectura),
    .out(Leer_Datos_1), .sel(Leer_Registro_1));
  Multiplexer #(.select(2), .width(8), .enable("false")) multiplexer_2 (
    .in0(registro_1_lectura), .in1(registro_2_lectura), .in2(registro_3_lectura), .in3(registro_4_lectura),
    .out(Leer_Datos_2), .sel(Leer_Registro_2));
endmodule

module ALU_con_Banco_de_Registros (
  input  [17:0] Escribe,
  input  Reloj,
  output [7:0] Salida,
  output Desborde
);

  wire [7:0] banco_de_registros_1_leer_datos_1, banco_de_registros_1_leer_datos_2, multiplexer_1_out;

  Multiplexer #(.width(8), .enable("false")) multiplexer_1 (
    .in0(banco_de_registros_1_leer_datos_2), .in1(Escribe[9:2]), .out(multiplexer_1_out), .sel(Escribe[12]));
  Banco_de_Registros banco_de_registros_1 (
    .Reloj(Reloj), .Leer_Datos_1(banco_de_registros_1_leer_datos_1),
    .Leer_Datos_2(banco_de_registros_1_leer_datos_2), .Escribir_Datos(Salida), .Escribir(1'b1),
    .Escribir_Registro(Escribe[1:0]), .Leer_Registro_1(Escribe[14:13]), .Leer_Registro_2(Escribe[11:10]));
  ALU_8_bits_completa_uso alu_8_bits_completa_uso_1 (
    .Operacion(Escribe[17:15]), .Salida(Salida), .A(banco_de_registros_1_leer_datos_1),
    .B(multiplexer_1_out), .Desborde(Desborde));
endmodule

module ALU_con_Banco_Uso (
  input  [17:0] Entrada,
  input  Reloj,
  output [7:0] Salida,
  output Desbordamiento
);

  ALU_con_Banco_de_Registros alu_con_banco_de_registros_1 (
    .Escribe(Entrada), .Reloj(Reloj), .Salida(Salida), .Desborde(Desbordamiento));
endmodule
